// Logisim project mct4.circ as structural Verilog: 2 circuits, main circuit main
module main (
  input  in_1,
  input  in_2
);

  wire and_1_out, apu_1_carry, Clock_out, comparator_1_eq, dipswitch_2_sw1, dipswitch_2_sw2, dipswitch_2_sw3,
       dipswitch_2_sw4, dipswitch_2_sw5, dipswitch_2_sw6, dipswitch_2_sw7, dipswitch_2_sw8, dipswitch_2_sw9,
       dipswitch_2_sw10, dipswitch_2_sw11, dipswitch_2_sw12, dipswitch_2_sw13, Reset_out;
  wire [3:0] controlled_buffer_1_out, MAR_q, PC_q;
  wire [7:0] A_q, apu_1_sum, B_q, IR_q, ram_1_dout, undriven;
  wire [7:4] controlled_buffer_1_out_2;

  RAM #(.addrWidth(4), .enables("line")) ram_1 (
    .addr(MAR_q), .we(dipswitch_2_sw6), .clk(Clock_out),
    .din({controlled_buffer_1_out_2, controlled_buffer_1_out}), .dout(ram_1_dout));
  Register #(.width(4)) MAR (
    .D(controlled_buffer_1_out), .en(dipswitch_2_sw8), .clk(Clock_out), .Q(MAR_q), .clr(Reset_out));
  Register IR (
    .D({controlled_buffer_1_out_2, controlled_buffer_1_out}), .en(dipswitch_2_sw4), .clk(Clock_out),
    .Q(IR_q), .clr(Reset_out));
  assign {controlled_buffer_1_out_2, controlled_buffer_1_out} = dipswitch_2_sw7 ? ram_1_dout : 8'bz;  // Controlled_Buffer controlled_buffer_1
  assign {controlled_buffer_1_out_2, controlled_buffer_1_out} = dipswitch_2_sw5 ? {4'b0000, IR_q[3:0]} : 8'bz;  // Controlled_Buffer controlled_buffer_2
  Button Reset (.out(Reset_out));
  Button Clock (.out(Clock_out));
  LedBar ledbar_1 (
    .led0(controlled_buffer_1_out_2[7]), .led1(controlled_buffer_1_out_2[6]),
    .led2(controlled_buffer_1_out_2[5]), .led3(controlled_buffer_1_out_2[4]),
    .led4(controlled_buffer_1_out[3]), .led5(controlled_buffer_1_out[2]), .led6(controlled_buffer_1_out[1]),
    .led7(controlled_buffer_1_out[0]));
  // DipSwitch dipswitch_1: pin names not known
  assign {controlled_buffer_1_out_2, controlled_buffer_1_out} = in_1 ? undriven : 8'bz;  // Controlled_Buffer controlled_buffer_3
  Register A (
    .D({controlled_buffer_1_out_2, controlled_buffer_1_out}), .en(dipswitch_2_sw9), .clk(Clock_out), .Q(A_q),
    .clr(Reset_out));
  Register B (
    .D({controlled_buffer_1_out_2, controlled_buffer_1_out}), .en(dipswitch_2_sw11), .clk(Clock_out),
    .Q(B_q), .clr(Reset_out));
  DipSwitch #(.number(13)) dipswitch_2 (
    .sw1(dipswitch_2_sw1), .sw2(dipswitch_2_sw2), .sw3(dipswitch_2_sw3), .sw4(dipswitch_2_sw4),
    .sw5(dipswitch_2_sw5), .sw6(dipswitch_2_sw6), .sw7(dipswitch_2_sw7), .sw8(dipswitch_2_sw8),
    .sw9(dipswitch_2_sw9), .sw10(dipswitch_2_sw10), .sw11(dipswitch_2_sw11), .sw12(dipswitch_2_sw12),
    .sw13(dipswitch_2_sw13));
  assign {controlled_buffer_1_out_2, controlled_buffer_1_out} = dipswitch_2_sw10 ? A_q : 8'bz;  // Controlled_Buffer controlled_buffer_4
  assign {controlled_buffer_1_out_2, controlled_buffer_1_out} = dipswitch_2_sw12 ? apu_1_sum : 8'bz;  // Controlled_Buffer controlled_buffer_5
  assign {controlled_buffer_1_out_2, controlled_buffer_1_out} = in_2 ? {4'b0000, PC_q} : 8'bz;  // Controlled_Buffer controlled_buffer_6
  Counter #(.max('hf), .width(4)) PC (
    .clr(Reset_out), .load(dipswitch_2_sw2), .up(1'b1), .count(dipswitch_2_sw3), .clk(Clock_out),
    .D(controlled_buffer_1_out), .Q(PC_q));  // open: carry
  apu apu_1 (.A(A_q), .B(B_q), .AS(dipswitch_2_sw13), .sum(apu_1_sum), .carry(apu_1_carry));
  D_Flip_Flop Carry (.D(apu_1_carry), .clk(and_1_out), .reset(Reset_out));  // open: Q, Qn, preset
  D_Flip_Flop Zero (.D(comparator_1_eq), .clk(and_1_out), .reset(Reset_out));  // open: Q, Qn, preset
  Comparator comparator_1 (.a(apu_1_sum), .b({8{1'b0}}), .eq(comparator_1_eq));  // open: gt, lt
  and and_1 (and_1_out, Clock_out, dipswitch_2_sw12);
endmodule

module apu (
  input  [7:0] A,
  input  [7:0] B,
  input  AS,
  output [7:0] sum,
  output carry
);

  wire adder_1_cout, subtractor_1_bout;
  wire [7:0] adder_1_out, subtractor_1_out;

  Adder adder_1 (.a(A), .b(B), .out(adder_1_out), .cout(adder_1_cout));  // open: cin
  Subtractor subtractor_1 (.a(A), .b(B), .out(subtractor_1_out), .bout(subtractor_1_bout));  // open: bin
  Multiplexer #(.width(8)) multiplexer_1 (.in0(adder_1_out), .in1(subtractor_1_out), .out(sum), .sel(AS));
  Multiplexer multiplexer_2 (.in0(adder_1_cout), .in1(subtractor_1_bout), .out(carry), .sel(AS));
endmodule
